# Fritzing sketch Electric-Valve-Command (saved by Fritzing 0.9.3b)
breadboards: 1

parts:
  U1 = ESP32-38PinWide [part_number=ESP32-38PinWide]
  U2 = LM2596 step down module
  YF-S201_Flow_Meter1 = YF-S201 Water Flow Meter  # not connected
  VALVE1 = Plastic Solenoid Valve
  Part1 = OMRON PCB Power Relay – G5LE [part_number="G5LE-1\r\n" package=THT]

nets:
  N1: U1.3.3, U2.OUT+
  N2: U2.IN-, U2.OUT-
  N3: VALVE1.no_name_yet#2, Part1.B

notes:
  Home Source Of Power (200-240V)
  AC/DC Adaptor modal: NBS36C120250HE
  Outputs 12V == 2.5A
  Adjustment of the potentiometer for an output of 3.3V
  IN
  Normally this one in inline with the GRN pin in our Relay (it's the middle one)

custom parts:
  ESP32-38PinWide: Generic 38-Pin ESP32 with wide format (only access to one side of pins on a breadboard) based on Stephen Lilley's HiLetgo ESP-WROOM-32 ESP32 ESP-32S Development Board.
  LM2596 step down module: LM2596 DC-DC step down power supply module 3 A.
  YF-S201 Water Flow Meter: The YF-S201 Flow Meter. The input voltage is 5V to 24V (DC).

// code stored in the sketch: Test-Electrovane.ino
 #define RELAY_PIN 25 // ESP32 pin GPIO16 connected to the electromagnetic lock via the relay

// the setup function runs once when you press reset or power the board
void setup() {
  // initialize digital pin GPIO16 as an output.
  pinMode(RELAY_PIN, OUTPUT);
}

// the loop function runs over and over again forever
void loop() {
  digitalWrite(RELAY_PIN, HIGH); // lock the door
  delay(4000);
  digitalWrite(RELAY_PIN, LOW);  // unlock the door
  delay(4000);
}
