# Fritzing sketch Electric-Valve-Push-Button (saved by Fritzing 0.9.3b)
breadboards: 1

parts:
  U3 = ESP32-38PinWide [part_number=ESP32-38PinWide]
  U4 = LM2596 step down module
  Part2 = OMRON PCB Power Relay – G5LE [part_number="G5LE-1\r\n" package=THT]
  VALVE2 = Plastic Solenoid Valve
  S2 = Pushbutton [package="[SMD]"]

nets:
  N1: U3.3.3, U4.OUT+
  N2: U3.GPIO26, U3.GPIO11, S2.Pin_1, S2.Pin_2, S2.Pin_3, S2.Pin_4
  N3: U4.IN-, U4.OUT-
  N4: Part2.B, VALVE2.no_name_yet#2

notes:
  Home Source Of Power (200-240V)
  AC/DC Adaptor modal: NBS36C120250HE
  Outputs 12V == 2.5A
  Adjustment of the potentiometer for an output of 3.3V
  IN
  Normally this one in inline with the GRN pin in our Relay (it's the middle one)

custom parts:
  ESP32-38PinWide: Generic 38-Pin ESP32 with wide format (only access to one side of pins on a breadboard) based on Stephen Lilley's HiLetgo ESP-WROOM-32 ESP32 ESP-32S Development Board.
  LM2596 step down module: LM2596 DC-DC step down power supply module 3 A.
