# Fritzing sketch Final-Valve-Push-ThingSpeak-Flow (saved by Fritzing 0.9.3b)
breadboards: 1

parts:
  U3 = ESP32-38PinWide [part_number=ESP32-38PinWide]
  U4 = LM2596 step down module
  Part2 = OMRON PCB Power Relay – G5LE [part_number="G5LE-1\r\n" package=THT]
  VALVE2 = Plastic Solenoid Valve
  S2 = Pushbutton [package="[SMD]"]
  YF-S201_Flow_Meter1 = YF-S201 Water Flow Meter
  LED1 = smd LED [color="Red (633nm)" package="0805 [SMD]"]
  LED2 = smd LED [color="Red (633nm)" package="0603 [SMD]"]

nets:
  N1: U3.3.3, U4.OUT+, Part2.COIL2, YF-S201_Flow_Meter1.VCC
  N2: U3.GPIO26, U3.GPIO11, Part2.C, S2.Pin_1, S2.Pin_2, S2.Pin_3, S2.Pin_4, YF-S201_Flow_Meter1.GND, LED1.cathode, LED2.cathode
  N3: U3.GPIO2, YF-S201_Flow_Meter1.SIG
  N4: U3.GPIO4, LED1.anode
  N5: U3.GPIO16, LED2.anode
  N6: U4.IN-, U4.OUT-
  N7: Part2.B, VALVE2.no_name_yet#2

notes:
  Home Source Of Power (200-240V)
  AC/DC Adaptor modal: NBS36C120250HE
  Outputs 12V == 2.5A
  Adjustment of the potentiometer for an output of 5V
  IN
  Normally this one in inline with the GRN pin in our Relay (it's the middle one)
  Command Pin (in the right side blue one)
  In the code it's connected to pin 5 and it's a Green Led.

custom parts:
  ESP32-38PinWide: Generic 38-Pin ESP32 with wide format (only access to one side of pins on a breadboard) based on Stephen Lilley's HiLetgo ESP-WROOM-32 ESP32 ESP-32S Development Board.
  LM2596 step down module: LM2596 DC-DC step down power supply module 3 A.
  YF-S201 Water Flow Meter: The YF-S201 Flow Meter. The input voltage is 5V to 24V (DC).
